// Logisim project MaryLadder_8bits_sim.circ as structural Verilog: 1 circuit, main circuit main
module main (
);

  wire and_1_out, and_2_out, and_3_out, and_4_out, dipswitch_1_sw1, dipswitch_1_sw2, dipswitch_1_sw3,
       dipswitch_1_sw4, dipswitch_1_sw5, dipswitch_1_sw6, dipswitch_1_sw7, dipswitch_1_sw8, dipswitch_2_sw1,
       dipswitch_2_sw2, dipswitch_2_sw3, dipswitch_2_sw4, dipswitch_2_sw5, dipswitch_2_sw6, dipswitch_2_sw7,
       dipswitch_2_sw8, or_1_out, or_2_out, undriven, undriven_2, undriven_3, undriven_4, undriven_5,
       xor_1_out, xor_2_out, xor_3_out, xor_4_out;

  LED led_1 (.in(dipswitch_1_sw1));
  LED led_2 (.in(dipswitch_2_sw1));
  LED led_3 (.in(dipswitch_1_sw2));
  LED led_4 (.in(dipswitch_1_sw3));
  DipSwitch dipswitch_1 (
    .sw1(dipswitch_1_sw1), .sw2(dipswitch_1_sw2), .sw3(dipswitch_1_sw3), .sw4(dipswitch_1_sw4),
    .sw5(dipswitch_1_sw5), .sw6(dipswitch_1_sw6), .sw7(dipswitch_1_sw7), .sw8(dipswitch_1_sw8));
  LED led_5 (.in(dipswitch_2_sw2));
  LED led_6 (.in(dipswitch_2_sw3));
  DipSwitch dipswitch_2 (
    .sw1(dipswitch_2_sw1), .sw2(dipswitch_2_sw2), .sw3(dipswitch_2_sw3), .sw4(dipswitch_2_sw4),
    .sw5(dipswitch_2_sw5), .sw6(dipswitch_2_sw6), .sw7(dipswitch_2_sw7), .sw8(dipswitch_2_sw8));
  LED led_7 (.in(dipswitch_1_sw4));
  LED led_8 (.in(dipswitch_1_sw5));
  LED led_9 (.in(dipswitch_1_sw6));
  LED led_10 (.in(dipswitch_2_sw4));
  LED led_11 (.in(dipswitch_2_sw5));
  LED led_12 (.in(dipswitch_2_sw6));
  LED led_13 (.in(dipswitch_1_sw7));
  LED led_14 (.in(dipswitch_1_sw8));
  LED led_15 (.in(dipswitch_2_sw7));
  LED led_16 (.in(dipswitch_2_sw8));
  xor xor_1 (xor_1_out, undriven, undriven_2);
  xor xor_2 (xor_2_out, undriven_3, undriven_4);
  _7_Segment_Display u_7_segment_display_1 ();  // open: g, f, a, b, e, d, c, dp
  xor xor_3 (xor_3_out, xor_1_out, undriven_5);
  and and_1 (and_1_out, undriven_5, xor_1_out);
  or or_1 (or_1_out, and_1_out, and_2_out);
  and and_2 (and_2_out, undriven_2, undriven);
  xor xor_4 (xor_4_out, xor_2_out, or_1_out);
  and and_3 (and_3_out, or_1_out, xor_2_out);
  or or_2 (or_2_out, and_3_out, and_4_out);
  and and_4 (and_4_out, undriven_4, undriven_3);
  _7_Segment_Display u_7_segment_display_2 ();  // open: g, f, a, b, e, d, c, dp
  _7_Segment_Display u_7_segment_display_3 ();  // open: g, f, a, b, e, d, c, dp

  // Notes on the sheet:
  //   A7
  //   128
  //   B7
  //   128
  //   A6
  //   A5
  //   64
  //   32
  //   16
  //   B6
  //   B5
  //   64
  //   32
  //   16
  //   [1st Input]
  //   A
  //   A4
  //   A3
  //   A2
  //   8
  //   4
  //   [2nd Input]
  //   B
  //   B4
  //   B3
  //   B2
  //   8
  //   4
  //   A1
  //   A0
  //   2
  //   1
  //   B1
  //   B0
  //   2
  //   1
  //   A0
  //   K
  //   XB0
  //   S0
endmodule
